// Logisim project CRC.circ as structural Verilog
module CRC (
  input  [7:0] A,
  input  [3:0] B,
  output [10:0] C
);

  wire _0, _1, _2, _3, _4, _5, _6, ans3, ans4, ans5, ans6, ans7, ans8, ans9, ans10;
  wire [2:0] n4bitdiv_1_remainder, n4bitdiv_2_remainder, n4bitdiv_3_remainder, n4bitdiv_4_remainder,
       n4bitdiv_5_remainder, n4bitdiv_6_remainder;
  wire [3:0] _7_10;
  wire [3:1] the_m;
  wire [10:0] bit_extender_1_out;

  assign bit_extender_1_out = {{3{1'b0}}, A};  // Bit_Extender bit_extender_1
  Shifter #(.width(11)) shifter_1 (
    .in(bit_extender_1_out), .\dist (4'b0011), .out({_7_10, _6, _5, _4, _3, _2, _1, _0}));
  _4bitDiv u_4bitdiv_1 (.dividend(_7_10), .divisor(B), .remainder(n4bitdiv_1_remainder), .ans(ans10));
  _4bitDiv u_4bitdiv_2 (.dividend({the_m, _3}), .divisor(B), .remainder(n4bitdiv_2_remainder), .ans(ans6));
  _4bitDiv u_4bitdiv_3 (
    .dividend({n4bitdiv_1_remainder, _6}), .divisor(B), .remainder(n4bitdiv_3_remainder), .ans(ans9));
  _4bitDiv u_4bitdiv_4 (
    .dividend({n4bitdiv_2_remainder, _2}), .divisor(B), .remainder(n4bitdiv_4_remainder), .ans(ans5));
  _4bitDiv u_4bitdiv_5 (
    .dividend({n4bitdiv_3_remainder, _5}), .divisor(B), .remainder(n4bitdiv_5_remainder), .ans(ans8));
  _4bitDiv u_4bitdiv_6 (
    .dividend({n4bitdiv_4_remainder, _1}), .divisor(B), .remainder(n4bitdiv_6_remainder), .ans(ans4));
  _4bitDiv u_4bitdiv_7 (.dividend({n4bitdiv_5_remainder, _4}), .divisor(B), .remainder(the_m), .ans(ans7));
  _4bitDiv u_4bitdiv_8 (.dividend({n4bitdiv_6_remainder, _0}), .divisor(B), .remainder(C[2:0]), .ans(ans3));

  assign C[10:3] = A;

  // Other names for the same wires on the sheet: ans0_2[2:0] = C[2:0]; origin[7:0] = A; divisor[3:0] = B;
  //   the_m[0] = _3
endmodule

module _4bitDiv (
  input  [3:0] dividend,
  input  [3:0] divisor,
  output [2:0] remainder,
  output ans
);

  wire [3:0] multiplexer_1_out, res;

  assign res = dividend ^ divisor;  // XOR_Gate xor_1, 4 bits wide
  Multiplexer #(.width(4)) multiplexer_1 (
    .in0(dividend), .in1(res), .out(multiplexer_1_out), .sel(dividend[3]));  // open: en
  Bit_Extender #(.in_width(4), .out_width(3)) bit_extender_1 (.in(multiplexer_1_out), .out(remainder));

  assign ans = dividend[3];

  // Other names for the same wires on the sheet: h_d = dividend[3]
endmodule
