// Logisim project grf.circ as structural Verilog
module registerMap (
  input  clk,
  input  reset,
  input  en,
  input  [4:0] address,
  input  [4:0] address1,
  input  [4:0] address2,
  input  [31:0] in,
  output [31:0] out1,
  output [31:0] out2
);

  wire [31:0] _0, _1, _2, _3, _4, _5, _6, _7, _8, _9, _10, _11, _12, _13, _14, _15, _16, _17, _18, _19, _20,
       _21, _22, _23, _24, _25, _26, _27, _28, _29, _30, _31, a0, a1, a2, a3, a4, a5, a6, a7, a8, a9, a10,
       a11, a12, a13, a14, a15, a16, a17, a18, a19, a20, a21, a22, a23, a24, a25, a26, a27, a28, a29, a30,
       a31;

  Demultiplexer #(.select(5), .width(32), .tristate("true")) demultiplexer_1 (
    .out0(_0), .out1(_1), .out2(_2), .out3(_3), .out4(_4), .out5(_5), .out6(_6), .out7(_7), .out8(_8),
    .out9(_9), .out10(_10), .out11(_11), .out12(_12), .out13(_13), .out14(_14), .out15(_15), .out16(_16),
    .out17(_17), .out18(_18), .out19(_19), .out20(_20), .out21(_21), .out22(_22), .out23(_23), .out24(_24),
    .out25(_25), .out26(_26), .out27(_27), .out28(_28), .out29(_29), .out30(_30), .out31(_31), .in(in),
    .sel(address));  // open: en
  Register #(.width(32)) u__0 (.en(en), .Q(a0), .clk(clk), .clr(reset));  // open: D
  Register #(.width(32)) u__4 (.D(_4), .en(en), .Q(a4), .clk(clk), .clr(reset));
  Register #(.width(32)) u__8 (.D(_8), .en(en), .Q(a8), .clk(clk), .clr(reset));
  Register #(.width(32)) u__12 (.D(_12), .en(en), .Q(a12), .clk(clk), .clr(reset));
  Register #(.width(32)) u__16 (.D(_16), .en(en), .Q(a16), .clk(clk), .clr(reset));
  Register #(.width(32)) u__20 (.D(_20), .en(en), .Q(a20), .clk(clk), .clr(reset));
  Register #(.width(32)) u__24 (.D(_24), .en(en), .Q(a24), .clk(clk), .clr(reset));
  Register #(.width(32)) u__28 (.D(_28), .en(en), .Q(a28), .clk(clk), .clr(reset));
  Register #(.width(32)) u__1 (.D(_1), .en(en), .Q(a1), .clk(clk), .clr(reset));
  Register #(.width(32)) u__5 (.D(_5), .en(en), .Q(a5), .clk(clk), .clr(reset));
  Register #(.width(32)) u__9 (.D(_9), .en(en), .Q(a9), .clk(clk), .clr(reset));
  Register #(.width(32)) u__13 (.D(_13), .en(en), .Q(a13), .clk(clk), .clr(reset));
  Register #(.width(32)) u__17 (.D(_17), .en(en), .Q(a17), .clk(clk), .clr(reset));
  Register #(.width(32)) u__21 (.D(_21), .en(en), .Q(a21), .clk(clk), .clr(reset));
  Register #(.width(32)) u__25 (.D(_25), .en(en), .Q(a25), .clk(clk), .clr(reset));
  Register #(.width(32)) u__29 (.D(_29), .en(en), .Q(a29), .clk(clk), .clr(reset));
  Register #(.width(32)) u__2 (.D(_2), .en(en), .Q(a2), .clk(clk), .clr(reset));
  Register #(.width(32)) u__6 (.D(_6), .en(en), .Q(a6), .clk(clk), .clr(reset));
  Register #(.width(32)) u__10 (.D(_10), .en(en), .Q(a10), .clk(clk), .clr(reset));
  Register #(.width(32)) u__14 (.D(_14), .en(en), .Q(a14), .clk(clk), .clr(reset));
  Register #(.width(32)) u__18 (.D(_18), .en(en), .Q(a18), .clk(clk), .clr(reset));
  Register #(.width(32)) u__22 (.D(_22), .en(en), .Q(a22), .clk(clk), .clr(reset));
  Register #(.width(32)) u__26 (.D(_26), .en(en), .Q(a26), .clk(clk), .clr(reset));
  Register #(.width(32)) u__30 (.D(_30), .en(en), .Q(a30), .clk(clk), .clr(reset));
  Register #(.width(32)) u__3 (.D(_3), .en(en), .Q(a3), .clk(clk), .clr(reset));
  Register #(.width(32)) u__7 (.D(_7), .en(en), .Q(a7), .clk(clk), .clr(reset));
  Register #(.width(32)) u__11 (.D(_11), .en(en), .Q(a11), .clk(clk), .clr(reset));
  Register #(.width(32)) u__15 (.D(_15), .en(en), .Q(a15), .clk(clk), .clr(reset));
  Register #(.width(32)) u__19 (.D(_19), .en(en), .Q(a19), .clk(clk), .clr(reset));
  Register #(.width(32)) u__23 (.D(_23), .en(en), .Q(a23), .clk(clk), .clr(reset));
  Register #(.width(32)) u__27 (.D(_27), .en(en), .Q(a27), .clk(clk), .clr(reset));
  Register #(.width(32)) u__31 (.D(_31), .en(en), .Q(a31), .clk(clk), .clr(reset));
  Multiplexer #(.select(5), .width(32)) multiplexer_1 (
    .in0(a0), .in1(a1), .in2(a2), .in3(a3), .in4(a4), .in5(a5), .in6(a6), .in7(a7), .in8(a8), .in9(a9),
    .in10(a10), .in11(a11), .in12(a12), .in13(a13), .in14(a14), .in15(a15), .in16(a16), .in17(a17),
    .in18(a18), .in19(a19), .in20(a20), .in21(a21), .in22(a22), .in23(a23), .in24(a24), .in25(a25),
    .in26(a26), .in27(a27), .in28(a28), .in29(a29), .in30(a30), .in31(a31), .out(out1), .sel(address1));  // open: en
  Multiplexer #(.select(5), .width(32)) multiplexer_2 (
    .in0(a0), .in1(a1), .in2(a2), .in3(a3), .in4(a4), .in5(a5), .in6(a6), .in7(a7), .in8(a8), .in9(a9),
    .in10(a10), .in11(a11), .in12(a12), .in13(a13), .in14(a14), .in15(a15), .in16(a16), .in17(a17),
    .in18(a18), .in19(a19), .in20(a20), .in21(a21), .in22(a22), .in23(a23), .in24(a24), .in25(a25),
    .in26(a26), .in27(a27), .in28(a28), .in29(a29), .in30(a30), .in31(a31), .out(out2), .sel(address2));  // open: en

  // Other names for the same wires on the sheet: address3[4:0] = address
endmodule

module grf (
  input  clk,
  input  clr,
  input  WE,
  input  [4:0] A1,
  input  [4:0] A2,
  input  [4:0] A3,
  input  [31:0] WD,
  output [31:0] RD1,
  output [31:0] RD2
);

  // registerMap registermap_1: pin names not known; wires that end beside it: clk, clr, WE, A3, A1, A2, WD, RD1, RD2

  // Other names for the same wires on the sheet: address1[4:0] = A1; address2[4:0] = A2; address3[4:0] = A3; en = WE;
  //   in[31:0] = WD; out1[31:0] = RD1; out2[31:0] = RD2; reset = clr
endmodule
