// Logisim project navigation.circ as structural Verilog
module navigation (
  input  [1:0] dir,
  input  clk,
  input  reset,
  output arrive,
  output hit
);

  wire transform_1_hit;
  wire [2:0] register_1_q, transform_1_location_l;

  transform transform_1 (
    .location_f(register_1_q), .dir(dir), .location_l(transform_1_location_l), .hit(transform_1_hit));
  Register #(.width(3)) register_1 (.D(transform_1_location_l), .Q(register_1_q), .clk(clk), .clr(reset));  // open: en
  Register #(.width(1)) register_2 (.D(transform_1_hit), .Q(hit), .clk(clk), .clr(reset));  // open: en
  \output  output_1 (.location_f(register_1_q), .arrive(arrive));
endmodule

module transform (
  input  [2:0] location_f,
  input  [1:0] dir,
  output [2:0] location_l,
  output hit
);

  wire and_1_out, and_2_out, and_3_out, and_4_out, and_5_out, and_6_out, and_7_out, and_8_out, and_9_out,
       and_10_out, and_11_out, and_12_out, and_13_out, and_14_out, and_15_out, and_16_out, and_17_out,
       not_1_out, not_2_out, not_3_out, not_4_out, not_5_out, not_6_out, not_7_out, not_8_out, not_9_out,
       not_10_out, not_11_out, not_12_out, not_13_out, not_14_out, not_15_out, not_16_out, not_17_out,
       not_18_out, not_19_out, not_20_out, not_21_out, not_22_out, not_23_out, not_24_out, not_25_out,
       not_26_out, not_27_out, not_28_out, not_29_out, not_30_out, not_31_out, not_32_out, not_33_out,
       not_34_out, not_35_out, not_36_out, not_37_out;

  not not_1 (not_1_out, location_f[1]);
  not not_2 (not_2_out, dir[1]);
  not not_3 (not_3_out, location_f[1]);
  not not_4 (not_4_out, dir[0]);
  not not_5 (not_5_out, location_f[0]);
  not not_6 (not_6_out, dir[1]);
  not not_7 (not_7_out, location_f[1]);
  not not_8 (not_8_out, dir[1]);
  not not_9 (not_9_out, location_f[2]);
  not not_10 (not_10_out, location_f[1]);
  not not_11 (not_11_out, dir[1]);
  not not_12 (not_12_out, dir[0]);
  not not_13 (not_13_out, location_f[1]);
  not not_14 (not_14_out, location_f[0]);
  not not_15 (not_15_out, location_f[1]);
  not not_16 (not_16_out, dir[1]);
  not not_17 (not_17_out, location_f[1]);
  not not_18 (not_18_out, dir[0]);
  not not_19 (not_19_out, location_f[1]);
  not not_20 (not_20_out, dir[1]);
  not not_21 (not_21_out, dir[0]);
  not not_22 (not_22_out, location_f[0]);
  not not_23 (not_23_out, dir[1]);
  not not_24 (not_24_out, dir[0]);
  not not_25 (not_25_out, location_f[1]);
  not not_26 (not_26_out, dir[1]);
  not not_27 (not_27_out, location_f[1]);
  not not_28 (not_28_out, location_f[2]);
  not not_29 (not_29_out, location_f[1]);
  not not_30 (not_30_out, dir[1]);
  not not_31 (not_31_out, location_f[2]);
  not not_32 (not_32_out, location_f[1]);
  not not_33 (not_33_out, dir[0]);
  not not_34 (not_34_out, location_f[0]);
  not not_35 (not_35_out, location_f[1]);
  not not_36 (not_36_out, dir[1]);
  not not_37 (not_37_out, dir[0]);
  and and_1 (and_1_out, not_1_out, location_f[0], not_2_out);
  and and_2 (and_2_out, not_3_out, location_f[0], not_4_out);
  and and_3 (and_3_out, location_f[1], not_5_out, not_6_out, dir[0]);
  and and_4 (and_4_out, location_f[2], not_7_out, not_8_out, dir[0]);
  and and_5 (and_5_out, not_9_out, not_10_out, not_11_out, not_12_out);
  and and_6 (and_6_out, not_13_out, location_f[0], dir[1], dir[0]);
  and and_7 (and_7_out, location_f[1], not_14_out, dir[1], dir[0]);
  and and_8 (and_8_out, location_f[2], not_15_out, not_16_out, dir[0]);
  and and_9 (and_9_out, location_f[2], not_17_out, dir[1], not_18_out);
  and and_10 (and_10_out, not_19_out, location_f[0], not_20_out, not_21_out);
  and and_11 (and_11_out, location_f[1], not_22_out, not_23_out, not_24_out);
  and and_12 (and_12_out, location_f[2], not_25_out, not_26_out);
  and and_13 (and_13_out, location_f[2], not_27_out, dir[0]);
  and and_14 (and_14_out, not_28_out, not_29_out, not_30_out, dir[0]);
  and and_15 (and_15_out, not_31_out, not_32_out, dir[1], not_33_out);
  and and_16 (and_16_out, not_34_out, dir[1], dir[0]);
  and and_17 (and_17_out, location_f[2], not_35_out, not_36_out, not_37_out);
  or or_1 (location_l[0], and_1_out, and_2_out, and_3_out, and_4_out);
  or or_2 (location_l[1], and_5_out, and_6_out, and_7_out, and_8_out, and_9_out);
  or or_3 (location_l[2], and_10_out, and_11_out, and_12_out, and_13_out);
  or or_4 (hit, and_14_out, and_15_out, and_16_out, and_17_out);
endmodule

module \output  (
  input  [2:0] location_f,
  output arrive
);

  and and_1 (arrive, location_f[0], location_f[1]);
endmodule

module \transform胡乱排错误版  (
  input  l0,
  input  l1,
  input  l2,
  input  d0,
  input  d1,
  output L0_2,
  output L1_2,
  output L2_2,
  output hit
);

  wire and_1_out, and_2_out, and_3_out, and_4_out, and_5_out, and_6_out, and_7_out, and_8_out, and_9_out,
       and_10_out, and_11_out, and_12_out, and_13_out, and_14_out, and_15_out, and_16_out, and_17_out,
       not_1_out, not_2_out, not_3_out, not_4_out, not_5_out, not_6_out, not_7_out, not_8_out, not_9_out,
       not_10_out, not_11_out, not_12_out, not_13_out, not_14_out, not_15_out, not_16_out, not_17_out,
       not_18_out, not_19_out, not_20_out, not_21_out, not_22_out, not_23_out, not_24_out, not_25_out,
       not_26_out, not_27_out, not_28_out, not_29_out, not_30_out, not_31_out, not_32_out, not_33_out,
       not_34_out, not_35_out, not_36_out, not_37_out;

  not not_1 (not_1_out, l1);
  not not_2 (not_2_out, d0);
  not not_3 (not_3_out, d1);
  not not_4 (not_4_out, l2);
  not not_5 (not_5_out, d0);
  not not_6 (not_6_out, d1);
  not not_7 (not_7_out, l1);
  not not_8 (not_8_out, d0);
  not not_9 (not_9_out, l1);
  not not_10 (not_10_out, l0);
  not not_11 (not_11_out, l1);
  not not_12 (not_12_out, d0);
  not not_13 (not_13_out, d1);
  not not_14 (not_14_out, l1);
  not not_15 (not_15_out, l2);
  not not_16 (not_16_out, l1);
  not not_17 (not_17_out, d0);
  not not_18 (not_18_out, l1);
  not not_19 (not_19_out, d1);
  not not_20 (not_20_out, l1);
  not not_21 (not_21_out, d0);
  not not_22 (not_22_out, l1);
  not not_23 (not_23_out, d1);
  not not_24 (not_24_out, l2);
  not not_25 (not_25_out, d0);
  not not_26 (not_26_out, l1);
  not not_27 (not_27_out, d0);
  not not_28 (not_28_out, l0);
  not not_29 (not_29_out, l1);
  not not_30 (not_30_out, d0);
  not not_31 (not_31_out, l0);
  not not_32 (not_32_out, l1);
  not not_33 (not_33_out, d1);
  not not_34 (not_34_out, l2);
  not not_35 (not_35_out, l1);
  not not_36 (not_36_out, d0);
  not not_37 (not_37_out, d1);
  and and_1 (and_1_out, not_1_out, l2, not_2_out, not_3_out);
  and and_2 (and_2_out, l1, not_4_out, not_5_out, not_6_out);
  and and_3 (and_3_out, l0, not_7_out, not_8_out);
  and and_4 (and_4_out, l0, not_9_out, d1);
  and and_5 (and_5_out, not_10_out, not_11_out, not_12_out, not_13_out);
  and and_6 (and_6_out, not_14_out, l2, d0, d1);
  and and_7 (and_7_out, l1, not_15_out, d0, d1);
  and and_8 (and_8_out, l0, not_16_out, not_17_out, d1);
  and and_9 (and_9_out, l0, not_18_out, d0, not_19_out);
  and and_10 (and_10_out, not_20_out, l2, not_21_out);
  and and_11 (and_11_out, not_22_out, l2, not_23_out);
  and and_12 (and_12_out, l1, not_24_out, not_25_out, d1);
  and and_13 (and_13_out, l0, not_26_out, not_27_out, d1);
  and and_14 (and_14_out, not_28_out, not_29_out, not_30_out, d1);
  and and_15 (and_15_out, not_31_out, not_32_out, d0, not_33_out);
  and and_16 (and_16_out, not_34_out, d0, d1);
  and and_17 (and_17_out, l0, not_35_out, not_36_out, not_37_out);
  or or_1 (L0_2, and_1_out, and_2_out, and_3_out, and_4_out);
  or or_2 (L1_2, and_5_out, and_6_out, and_7_out, and_8_out, and_9_out);
  or or_3 (L2_2, and_10_out, and_11_out, and_12_out, and_13_out);
  or or_4 (hit, and_14_out, and_15_out, and_16_out, and_17_out);
endmodule

module \transform胡乱排正序版  (
  input  l2,
  input  l1,
  input  l0,
  input  d1,
  input  d0,
  output L2_2,
  output L1_2,
  output L0_2,
  output hit
);

  wire and_1_out, and_2_out, and_3_out, and_4_out, and_5_out, and_6_out, and_7_out, and_8_out, and_9_out,
       and_10_out, and_11_out, and_12_out, and_13_out, and_14_out, and_15_out, and_16_out, and_17_out,
       not_1_out, not_2_out, not_3_out, not_4_out, not_5_out, not_6_out, not_7_out, not_8_out, not_9_out,
       not_10_out, not_11_out, not_12_out, not_13_out, not_14_out, not_15_out, not_16_out, not_17_out,
       not_18_out, not_19_out, not_20_out, not_21_out, not_22_out, not_23_out, not_24_out, not_25_out,
       not_26_out, not_27_out, not_28_out, not_29_out, not_30_out, not_31_out, not_32_out, not_33_out,
       not_34_out, not_35_out, not_36_out, not_37_out;

  not not_1 (not_1_out, l1);
  not not_2 (not_2_out, d0);
  not not_3 (not_3_out, l1);
  not not_4 (not_4_out, d1);
  not not_5 (not_5_out, l2);
  not not_6 (not_6_out, d0);
  not not_7 (not_7_out, l1);
  not not_8 (not_8_out, d0);
  not not_9 (not_9_out, l0);
  not not_10 (not_10_out, l1);
  not not_11 (not_11_out, d0);
  not not_12 (not_12_out, d1);
  not not_13 (not_13_out, l1);
  not not_14 (not_14_out, l2);
  not not_15 (not_15_out, l1);
  not not_16 (not_16_out, d0);
  not not_17 (not_17_out, l1);
  not not_18 (not_18_out, d1);
  not not_19 (not_19_out, l1);
  not not_20 (not_20_out, d0);
  not not_21 (not_21_out, d1);
  not not_22 (not_22_out, l2);
  not not_23 (not_23_out, d0);
  not not_24 (not_24_out, d1);
  not not_25 (not_25_out, l1);
  not not_26 (not_26_out, d0);
  not not_27 (not_27_out, l1);
  not not_28 (not_28_out, l0);
  not not_29 (not_29_out, l1);
  not not_30 (not_30_out, d0);
  not not_31 (not_31_out, l0);
  not not_32 (not_32_out, l1);
  not not_33 (not_33_out, d1);
  not not_34 (not_34_out, l2);
  not not_35 (not_35_out, l1);
  not not_36 (not_36_out, d0);
  not not_37 (not_37_out, d1);
  and and_1 (and_1_out, not_1_out, l2, not_2_out);
  and and_2 (and_2_out, not_3_out, l2, not_4_out);
  and and_3 (and_3_out, l1, not_5_out, not_6_out, d1);
  and and_4 (and_4_out, l0, not_7_out, not_8_out, d1);
  and and_5 (and_5_out, not_9_out, not_10_out, not_11_out, not_12_out);
  and and_6 (and_6_out, not_13_out, l2, d0, d1);
  and and_7 (and_7_out, l1, not_14_out, d0, d1);
  and and_8 (and_8_out, l0, not_15_out, not_16_out, d1);
  and and_9 (and_9_out, l0, not_17_out, d0, not_18_out);
  and and_10 (and_10_out, not_19_out, l2, not_20_out, not_21_out);
  and and_11 (and_11_out, l1, not_22_out, not_23_out, not_24_out);
  and and_12 (and_12_out, l0, not_25_out, not_26_out);
  and and_13 (and_13_out, l0, not_27_out, d1);
  and and_14 (and_14_out, not_28_out, not_29_out, not_30_out, d1);
  and and_15 (and_15_out, not_31_out, not_32_out, d0, not_33_out);
  and and_16 (and_16_out, not_34_out, d0, d1);
  and and_17 (and_17_out, l0, not_35_out, not_36_out, not_37_out);
  or or_1 (L2_2, and_1_out, and_2_out, and_3_out, and_4_out);
  or or_2 (L1_2, and_5_out, and_6_out, and_7_out, and_8_out, and_9_out);
  or or_3 (L0_2, and_10_out, and_11_out, and_12_out, and_13_out);
  or or_4 (hit, and_14_out, and_15_out, and_16_out, and_17_out);
endmodule

module \output胡乱排  (
  input  l2,
  input  l1,
  input  l0,
  output arrive
);

  and and_1 (arrive, l2, l1);
endmodule
