// Logisim project FSM.circ as structural Verilog
module fsm (
  input  [1:0] in,
  input  clr,
  output z
);

  wire clock_1_out, register_2_q;
  wire [1:0] register_1_q, transform_1_status_l;

  transform transform_1 (.status(register_1_q), .in(in), .status_l(transform_1_status_l));
  Clock clock_1 (.out(clock_1_out));
  Register #(.width(2)) register_1 (
    .D(transform_1_status_l), .Q(register_1_q), .clk(clock_1_out), .clr(register_2_q));  // open: en
  Register #(.width(1)) register_2 (.D(clr), .Q(register_2_q), .clk(clock_1_out), .clr(register_2_q));  // open: en
  \output  output_1 (.status(register_1_q), .in(in), .z(z));
endmodule

module transform (
  input  [1:0] status,
  input  [1:0] in,
  output [1:0] status_l
);

  wire and_1_out, and_2_out, and_3_out, and_4_out, not_1_out, not_2_out, not_3_out, not_4_out, not_5_out,
       not_6_out, not_7_out;

  not not_1 (not_1_out, in[1]);
  not not_2 (not_2_out, status[0]);
  not not_3 (not_3_out, in[0]);
  not not_4 (not_4_out, status[1]);
  not not_5 (not_5_out, in[0]);
  not not_6 (not_6_out, status[0]);
  not not_7 (not_7_out, in[0]);
  and and_1 (and_1_out, in[0], not_1_out);
  and and_2 (and_2_out, not_2_out, status[1], not_3_out);
  and and_3 (and_3_out, not_4_out, status[0], not_5_out);
  and and_4 (and_4_out, status[1], not_6_out, not_7_out);
  or or_1 (status_l[0], and_1_out, and_2_out);
  or or_2 (status_l[1], and_3_out, and_4_out);
endmodule

module \output  (
  input  [1:0] status,
  input  [1:0] in,
  output z
);

  wire not_1_out, not_2_out;

  not not_1 (not_1_out, status[0]);
  not not_2 (not_2_out, in[0]);
  and and_1 (z, status[1], not_1_out, not_2_out);
endmodule

module \transform顺序  (
  input  s0,
  input  s1,
  input  i0,
  input  i1,
  output S0_2,
  output S1_2
);

  wire and_1_out, and_2_out, and_3_out, and_4_out, not_1_out, not_2_out, not_3_out, not_4_out, not_5_out,
       not_6_out, not_7_out;

  and and_1 (and_1_out, i0, not_1_out);
  not not_1 (not_1_out, i1);
  not not_2 (not_2_out, s0);
  and and_2 (and_2_out, not_2_out, s1, not_3_out);
  not not_3 (not_3_out, i0);
  not not_4 (not_4_out, s1);
  and and_3 (and_3_out, not_4_out, s0, not_5_out);
  not not_5 (not_5_out, i0);
  not not_6 (not_6_out, s0);
  and and_4 (and_4_out, s1, not_6_out, not_7_out);
  not not_7 (not_7_out, i0);
  or or_1 (S0_2, and_1_out, and_2_out);
  or or_2 (S1_2, and_3_out, and_4_out);
endmodule

module \output修  (
  input  s0,
  input  s1,
  input  i0,
  input  i1,
  output z
);

  wire not_1_out, not_2_out;

  not not_1 (not_1_out, s0);
  and and_1 (z, s1, not_1_out, not_2_out);
  not not_2 (not_2_out, i0);
endmodule
