// Logisim project ftoi.circ as structural Verilog: 2 circuits, main circuit ftoi
module ftoi (
  input  [15:0] float,
  output [31:0] \int 
);

  wire comparator_1_eq, comparator_2_eq;
  wire [4:0] subtractor_1_out;
  wire [31:0] adder_1_out, bit_extender_1_out, multiplexer_1_out, multiplexer_2_out, negator_1_out,
       shifter_1_out, \符号移位_1_out ;

  assign bit_extender_1_out = {{22{1'b0}}, float[9:0]};  // Bit_Extender bit_extender_1
  Adder #(.width(32)) adder_1 (.a(32'h400), .b(bit_extender_1_out), .out(adder_1_out));  // open: cin, cout
  Multiplexer #(.width(32)) multiplexer_1 (
    .in0(adder_1_out), .in1(bit_extender_1_out), .out(multiplexer_1_out), .sel(comparator_1_eq));  // open: en
  Comparator #(.width(5)) comparator_1 (.a({5{1'b0}}), .b(float[14:10]), .eq(comparator_1_eq));  // open: gt, lt
  Subtractor #(.width(5)) subtractor_1 (.a(float[14:10]), .b(5'b01111), .out(subtractor_1_out));  // open: bin, bout
  \符号移位  \u_符号移位_1  (.\原数 (multiplexer_1_out), .\移位 (subtractor_1_out), .out(\符号移位_1_out ));
  Shifter #(.width(32), .shift("lr")) shifter_1 (.in(\符号移位_1_out ), .\dist (5'b01010), .out(shifter_1_out));
  Comparator #(.width(5)) comparator_2 (.a(float[14:10]), .b({5{1'b1}}), .eq(comparator_2_eq));  // open: gt, lt
  Multiplexer #(.width(32)) multiplexer_2 (
    .in0(shifter_1_out), .in1(negator_1_out), .out(multiplexer_2_out), .sel(float[15]));  // open: en
  Negator #(.width(32)) negator_1 (.in(shifter_1_out), .out(negator_1_out));
  Multiplexer #(.width(32)) multiplexer_3 (
    .in0(multiplexer_2_out), .in1({32{1'b0}}), .out(\int ), .sel(comparator_2_eq));  // open: en
endmodule

module \符号移位  (
  input  [31:0] \原数 ,
  input  [4:0] \移位 ,
  output [31:0] out
);

  wire [4:0] negator_1_out;
  wire [31:0] shifter_1_out, shifter_2_out;

  Negator #(.width(5)) negator_1 (.in(\移位 ), .out(negator_1_out));
  Shifter #(.width(32)) shifter_1 (.in(\原数 ), .\dist (\移位 ), .out(shifter_1_out));
  Shifter #(.width(32), .shift("lr")) shifter_2 (.in(\原数 ), .\dist (negator_1_out), .out(shifter_2_out));
  Multiplexer #(.width(32)) multiplexer_1 (
    .in0(shifter_1_out), .in1(shifter_2_out), .out(out), .sel(\移位 [4]));  // open: en
endmodule
