// Logisim project 编码电路.circ as structural Verilog
module \自己码  (
  input  l2,
  input  l1,
  input  l0,
  input  d1,
  input  d0,
  output L2_2,
  output L1_2,
  output L0_2,
  output hit
);

  wire and_1_out, and_2_out, and_3_out, and_4_out, and_5_out, and_6_out, and_7_out, and_8_out, and_9_out,
       and_10_out, and_11_out, and_12_out, and_13_out, and_14_out, and_15_out, and_16_out, and_17_out,
       not_1_out, not_2_out, not_3_out, not_4_out, not_5_out, not_6_out, not_7_out, not_8_out, not_9_out,
       not_10_out, not_11_out, not_12_out, not_13_out, not_14_out, not_15_out, not_16_out, not_17_out,
       not_18_out, not_19_out, not_20_out, not_21_out, not_22_out, not_23_out, not_24_out, not_25_out,
       not_26_out, not_27_out, not_28_out, not_29_out, not_30_out, not_31_out, not_32_out, not_33_out,
       not_34_out, not_35_out, not_36_out, not_37_out;

  not not_1 (not_1_out, l1);
  not not_2 (not_2_out, d1);
  not not_3 (not_3_out, d0);
  not not_4 (not_4_out, l0);
  not not_5 (not_5_out, d1);
  not not_6 (not_6_out, d0);
  not not_7 (not_7_out, l1);
  not not_8 (not_8_out, d1);
  not not_9 (not_9_out, l1);
  not not_10 (not_10_out, l2);
  not not_11 (not_11_out, l1);
  not not_12 (not_12_out, d1);
  not not_13 (not_13_out, d0);
  not not_14 (not_14_out, l1);
  not not_15 (not_15_out, l0);
  not not_16 (not_16_out, l1);
  not not_17 (not_17_out, d1);
  not not_18 (not_18_out, l1);
  not not_19 (not_19_out, d0);
  not not_20 (not_20_out, l1);
  not not_21 (not_21_out, d1);
  not not_22 (not_22_out, l1);
  not not_23 (not_23_out, d0);
  not not_24 (not_24_out, l0);
  not not_25 (not_25_out, d1);
  not not_26 (not_26_out, l1);
  not not_27 (not_27_out, d1);
  not not_28 (not_28_out, l2);
  not not_29 (not_29_out, l1);
  not not_30 (not_30_out, d1);
  not not_31 (not_31_out, l2);
  not not_32 (not_32_out, l1);
  not not_33 (not_33_out, d0);
  not not_34 (not_34_out, l0);
  not not_35 (not_35_out, l1);
  not not_36 (not_36_out, d1);
  not not_37 (not_37_out, d0);
  and and_1 (and_1_out, not_1_out, l0, not_2_out, not_3_out);
  and and_2 (and_2_out, l1, not_4_out, not_5_out, not_6_out);
  and and_3 (and_3_out, l2, not_7_out, not_8_out);
  and and_4 (and_4_out, l2, not_9_out, d0);
  and and_5 (and_5_out, not_10_out, not_11_out, not_12_out, not_13_out);
  and and_6 (and_6_out, not_14_out, l0, d1, d0);
  and and_7 (and_7_out, l1, not_15_out, d1, d0);
  and and_8 (and_8_out, l2, not_16_out, not_17_out, d0);
  and and_9 (and_9_out, l2, not_18_out, d1, not_19_out);
  and and_10 (and_10_out, not_20_out, l0, not_21_out);
  and and_11 (and_11_out, not_22_out, l0, not_23_out);
  and and_12 (and_12_out, l1, not_24_out, not_25_out, d0);
  and and_13 (and_13_out, l2, not_26_out, not_27_out, d0);
  and and_14 (and_14_out, not_28_out, not_29_out, not_30_out, d0);
  and and_15 (and_15_out, not_31_out, not_32_out, d1, not_33_out);
  and and_16 (and_16_out, not_34_out, d1, d0);
  and and_17 (and_17_out, l2, not_35_out, not_36_out, not_37_out);
  or or_1 (L2_2, and_1_out, and_2_out, and_3_out, and_4_out);
  or or_2 (L1_2, and_5_out, and_6_out, and_7_out, and_8_out, and_9_out);
  or or_3 (L0_2, and_10_out, and_11_out, and_12_out, and_13_out);
  or or_4 (hit, and_14_out, and_15_out, and_16_out, and_17_out);
endmodule

module \_8421码  (
  input  l2,
  input  l1,
  input  l0,
  input  d1,
  input  d0,
  output L2_2,
  output L1_2,
  output L0_2,
  output hit
);

  wire and_1_out, and_2_out, and_3_out, and_4_out, and_5_out, and_6_out, and_7_out, and_8_out, and_9_out,
       and_10_out, and_11_out, and_12_out, and_13_out, and_14_out, and_15_out, and_16_out, and_17_out,
       and_18_out, not_1_out, not_2_out, not_3_out, not_4_out, not_5_out, not_6_out, not_7_out, not_8_out,
       not_9_out, not_10_out, not_11_out, not_12_out, not_13_out, not_14_out, not_15_out, not_16_out,
       not_17_out, not_18_out, not_19_out, not_20_out, not_21_out, not_22_out, not_23_out, not_24_out,
       not_25_out, not_26_out, not_27_out, not_28_out;

  not not_1 (not_1_out, l0);
  not not_2 (not_2_out, d1);
  not not_3 (not_3_out, d0);
  not not_4 (not_4_out, d1);
  not not_5 (not_5_out, l1);
  not not_6 (not_6_out, d1);
  not not_7 (not_7_out, d1);
  not not_8 (not_8_out, d0);
  not not_9 (not_9_out, l0);
  not not_10 (not_10_out, d1);
  not not_11 (not_11_out, l0);
  not not_12 (not_12_out, d0);
  not not_13 (not_13_out, l2);
  not not_14 (not_14_out, l1);
  not not_15 (not_15_out, d1);
  not not_16 (not_16_out, d0);
  not not_17 (not_17_out, d0);
  not not_18 (not_18_out, l2);
  not not_19 (not_19_out, l0);
  not not_20 (not_20_out, d1);
  not not_21 (not_21_out, l2);
  not not_22 (not_22_out, l1);
  not not_23 (not_23_out, l0);
  not not_24 (not_24_out, l2);
  not not_25 (not_25_out, l0);
  not not_26 (not_26_out, d0);
  not not_27 (not_27_out, d1);
  not not_28 (not_28_out, d0);
  and and_1 (and_1_out, l1, not_1_out, not_2_out, not_3_out);
  and and_2 (and_2_out, l1, l0, not_4_out, d0);
  and and_3 (and_3_out, l2, l1);
  and and_4 (and_4_out, not_5_out, l0, not_6_out);
  and and_5 (and_5_out, l0, not_7_out, not_8_out);
  and and_6 (and_6_out, l1, not_9_out, not_10_out, d0);
  and and_7 (and_7_out, l1, not_11_out, d1, not_12_out);
  and and_8 (and_8_out, l1, l0, d1, d0);
  and and_9 (and_9_out, l2, l1);
  and and_10 (and_10_out, not_13_out, not_14_out, not_15_out, not_16_out);
  and and_11 (and_11_out, l0, d1, d0);
  and and_12 (and_12_out, l1, d1, d0);
  and and_13 (and_13_out, l1, l0, not_17_out);
  and and_14 (and_14_out, not_18_out, not_19_out, not_20_out, d0);
  and and_15 (and_15_out, not_21_out, not_22_out, not_23_out, d1);
  and and_16 (and_16_out, not_24_out, not_25_out, d1, not_26_out);
  and and_17 (and_17_out, l0, d1, d0);
  and and_18 (and_18_out, l1, l0, not_27_out, not_28_out);
  or or_1 (L2_2, and_1_out, and_2_out, and_3_out);
  or or_2 (L1_2, and_4_out, and_5_out, and_6_out, and_7_out, and_8_out, and_9_out);
  or or_3 (L0_2, and_10_out, and_11_out, and_12_out, and_13_out);
  or or_4 (hit, and_14_out, and_15_out, and_16_out, and_17_out, and_18_out);
endmodule

module \格雷码  (
  input  l2,
  input  l1,
  input  l0,
  input  d1,
  input  d0,
  output L2_2,
  output L1_2,
  output L0_2,
  output hit
);

  wire and_1_out, and_2_out, and_3_out, and_4_out, and_5_out, and_6_out, and_7_out, and_8_out, and_9_out,
       and_10_out, and_11_out, and_12_out, and_13_out, and_14_out, and_15_out, and_16_out, not_1_out,
       not_2_out, not_3_out, not_4_out, not_5_out, not_6_out, not_7_out, not_8_out, not_9_out, not_10_out,
       not_11_out, not_12_out, not_13_out, not_14_out, not_15_out, not_16_out, not_17_out, not_18_out,
       not_19_out, not_20_out, not_21_out, not_22_out, not_23_out, not_24_out, not_25_out, not_26_out,
       not_27_out, not_28_out;

  not not_1 (not_1_out, l2);
  not not_2 (not_2_out, d1);
  not not_3 (not_3_out, d0);
  not not_4 (not_4_out, l1);
  not not_5 (not_5_out, d1);
  not not_6 (not_6_out, l1);
  not not_7 (not_7_out, l1);
  not not_8 (not_8_out, d1);
  not not_9 (not_9_out, l2);
  not not_10 (not_10_out, d1);
  not not_11 (not_11_out, l2);
  not not_12 (not_12_out, d0);
  not not_13 (not_13_out, l1);
  not not_14 (not_14_out, d1);
  not not_15 (not_15_out, d0);
  not not_16 (not_16_out, l1);
  not not_17 (not_17_out, l2);
  not not_18 (not_18_out, l1);
  not not_19 (not_19_out, l0);
  not not_20 (not_20_out, l0);
  not not_21 (not_21_out, l1);
  not not_22 (not_22_out, l2);
  not not_23 (not_23_out, d1);
  not not_24 (not_24_out, l2);
  not not_25 (not_25_out, d0);
  not not_26 (not_26_out, l1);
  not not_27 (not_27_out, d1);
  not not_28 (not_28_out, d0);
  and and_1 (and_1_out, not_1_out, l0, not_2_out, not_3_out);
  and and_2 (and_2_out, l2, not_4_out, not_5_out);
  and and_3 (and_3_out, l2, not_6_out, d0);
  and and_4 (and_4_out, not_7_out, l0, not_8_out, d0);
  and and_5 (and_5_out, not_9_out, l1, not_10_out);
  and and_6 (and_6_out, not_11_out, l1, not_12_out);
  and and_7 (and_7_out, not_13_out, not_14_out, not_15_out);
  and and_8 (and_8_out, not_16_out, l0, d0);
  and and_9 (and_9_out, not_17_out, l1);
  and and_10 (and_10_out, l2, not_18_out);
  and and_11 (and_11_out, not_19_out, d0);
  and and_12 (and_12_out, not_20_out, d1);
  and and_13 (and_13_out, not_21_out, d1, d0);
  and and_14 (and_14_out, not_22_out, l1, not_23_out, d0);
  and and_15 (and_15_out, not_24_out, l1, d1, not_25_out);
  and and_16 (and_16_out, l2, not_26_out, not_27_out, not_28_out);
  or or_1 (L2_2, and_1_out, and_2_out, and_3_out);
  or or_2 (L1_2, and_4_out, and_5_out, and_6_out);
  or or_3 (L0_2, and_7_out, and_8_out, and_9_out, and_10_out);
  or or_4 (hit, and_11_out, and_12_out, and_13_out, and_14_out, and_15_out, and_16_out);
endmodule

module \独热码  (
  input  l4,
  input  l3,
  input  l2,
  input  l1,
  input  l0,
  input  d1,
  input  d0,
  output L4_2,
  output L3_2,
  output L2_2,
  output L1_2,
  output L0_2,
  output hit
);
endmodule

module navigation (
  input  [1:0] dir,
  input  clk,
  input  reset,
  output arrive,
  output hit
);

  wire A_out_8, arrive0, arrive1, arrive2, arrive3, hit0, hit1, hit2, hit3, hit4, hit5, hit6, hit7,
       \initial , location_1_out_10, location_1_out_11, location_2_out_8, location_2_out_10,
       location_2_out_11, location_3_out_8, location_3_out_9, multiplexer_1_out, or_1_out;

  Counter #(.width(1), .max('h1), .ongoal("stay")) counter_1 (
    .Q(\initial ), .clk(clk));  // open: load, D, count, carry, clr
  location location_1 (
    .out_9(hit3), .W(hit3), .out_10(location_1_out_10), .N(hit4), .out_8(hit4), .clk(clk), .reset(reset),
    .out_11(location_1_out_11), .S(location_2_out_8), .dir(dir));  // open: E
  location location_2 (
    .out_9(hit2), .W(hit2), .E(location_3_out_9), .out_10(location_2_out_10), .N(location_1_out_11),
    .out_8(location_2_out_8), .clk(clk), .reset(reset), .out_11(location_2_out_11), .S(A_out_8), .dir(dir));
  location A (
    .out_9(hit1), .W(hit1), .E(hit7), .out_10(hit7), .N(location_2_out_11), .out_8(A_out_8), .clk(clk),
    .reset(reset), .out_11(hit0), .S(multiplexer_1_out), .dir(dir));
  Multiplexer multiplexer_1 (.in0(1'b1), .in1(or_1_out), .out(multiplexer_1_out), .sel(\initial ));  // open: en
  or or_1 (or_1_out, hit0, arrive);
  location B (
    .out_9(arrive2), .W(location_1_out_10), .out_10(arrive1), .out_8(arrive0), .clk(clk), .reset(reset),
    .out_11(arrive3), .S(location_3_out_8), .dir(dir));  // open: E, N
  location location_3 (
    .out_9(location_3_out_9), .W(location_2_out_10), .E(hit5), .out_10(hit5), .out_8(location_3_out_8),
    .clk(clk), .reset(reset), .out_11(hit6), .S(hit6), .dir(dir));  // open: N
  or or_2 (arrive, arrive0, arrive1, arrive2, arrive3);
  or or_3 (hit, hit0, hit1, hit2, hit3, hit4, hit5, hit6, hit7);

  // Other names for the same wires on the sheet: re = reset
endmodule

module location (
  input  N,
  input  E,
  input  W,
  input  clk,
  input  [1:0] dir,
  input  reset,
  input  S,
  output out_8,
  output out_9,
  output out_10,
  output out_11
);

  wire or_1_out, register_1_q;

  or or_1 (or_1_out, E, S, W, N);
  Register #(.width(1)) register_1 (.D(or_1_out), .Q(register_1_q), .clk(clk), .clr(reset));  // open: en
  Demultiplexer #(.select(2)) demultiplexer_1 (
    .out0(out_8), .out1(out_10), .out2(out_11), .out3(out_9), .in(register_1_q), .sel(dir));  // open: en

  // Other names for the same wires on the sheet: outE = out_10; outN = out_8; outS = out_11; outW = out_9
endmodule
