// Logisim project MIPS-CPU.circ as structural Verilog
module main (
  input  in_1,
  output [31:0] out_2,
  output out_3,
  output [4:0] out_4,
  output [31:0] out_5,
  output out_6,
  output [4:0] out_7,
  output [31:0] out_8
);

  wire alu_1_zero, clk, instructionrecognition_1_add, instructionrecognition_1_addu,
       instructionrecognition_1_beq, instructionrecognition_1_j, instructionrecognition_1_jal,
       instructionrecognition_1_jr, instructionrecognition_1_lui, instructionrecognition_1_lw,
       instructionrecognition_1_or, instructionrecognition_1_ori, instructionrecognition_1_slt,
       instructionrecognition_1_sub, instructionrecognition_1_subu, instructionrecognition_1_sw,
       signalsender_1_bsel, signalsender_1_immextop;
  wire [1:0] RFWDSel, WRSel;
  wire [2:0] NPCOp;
  wire [3:0] signalsender_1_aluop;
  wire [4:0] instrcutionsplitter_1_rd, instrcutionsplitter_1_rs, instrcutionsplitter_1_rt;
  wire [5:0] instrcutionsplitter_1_funct, instrcutionsplitter_1_opcode;
  wire [15:0] instrcutionsplitter_1_imm16;
  wire [25:0] instrcutionsplitter_1_address, multiplexer_1_out;
  wire [31:0] dm_1_rd, ext_1_imm32, MemAddr, multiplexer_4_out, npc_2_npc, npc_2_pc4, pc_2_pc, rf_1_out1,
       shifter_1_out;

  // Probe on pc_2_pc
  // Probe on npc_2_npc
  // Probe on NPCOp
  Clock clock_1 (.out(clk));
  PC pc_2 (.NPC(npc_2_npc), .PC(pc_2_pc), .clk(clk), .clr(in_1));
  NPC npc_2 (
    .PC(pc_2_pc), .NPC(npc_2_npc), .imm26(multiplexer_1_out), .BeqYes(alu_1_zero), .NPCOp(NPCOp),
    .PC4(npc_2_pc4), .ra(rf_1_out1));
  Multiplexer #(.width(26)) multiplexer_1 (
    .in0({{10{1'b0}}, instrcutionsplitter_1_imm16}), .in1(instrcutionsplitter_1_address),
    .out(multiplexer_1_out), .sel(NPCOp[1]));  // open: en
  IM im_1 (.address(pc_2_pc), .instruction(out_2));
  InstrcutionSplitter instrcutionsplitter_1 (
    .instruction(out_2), .opcode(instrcutionsplitter_1_opcode), .rs(instrcutionsplitter_1_rs),
    .rt(instrcutionsplitter_1_rt), .rd(instrcutionsplitter_1_rd), .funct(instrcutionsplitter_1_funct),
    .imm16(instrcutionsplitter_1_imm16), .address(instrcutionsplitter_1_address));  // open: shamt
  Multiplexer #(.select(2), .width(5)) multiplexer_2 (
    .in0(instrcutionsplitter_1_rt), .in1(instrcutionsplitter_1_rd), .in2({5{1'b1}}), .out(out_4), .sel(WRSel));  // open: in3, en
  EXT ext_1 (.imm16(instrcutionsplitter_1_imm16), .imm32(ext_1_imm32), .ExtOp(signalsender_1_immextop));
  Multiplexer #(.select(2), .width(32)) multiplexer_3 (
    .in0(MemAddr), .in1(dm_1_rd), .in2(npc_2_pc4), .out(out_5), .sel(RFWDSel));  // open: in3, en
  InstructionRecognition instructionrecognition_1 (
    .opcode(instrcutionsplitter_1_opcode), .funct(instrcutionsplitter_1_funct),
    .ori(instructionrecognition_1_ori), .lw(instructionrecognition_1_lw), .sw(instructionrecognition_1_sw),
    .beq(instructionrecognition_1_beq), .j(instructionrecognition_1_j), .jal(instructionrecognition_1_jal),
    .addu(instructionrecognition_1_addu), .subu(instructionrecognition_1_subu),
    .slt(instructionrecognition_1_slt), .jr(instructionrecognition_1_jr), .lui(instructionrecognition_1_lui),
    .\or (instructionrecognition_1_or), .add(instructionrecognition_1_add), .sub(instructionrecognition_1_sub));
  RF rf_1 (
    .clk(clk), .reset(in_1), .en(out_3), .address1(instrcutionsplitter_1_rs),
    .address2(instrcutionsplitter_1_rt), .address3(out_4), .in(out_5), .out1(rf_1_out1), .out2(out_8));
  SignalSender signalsender_1 (
    .addu(instructionrecognition_1_addu), .subu(instructionrecognition_1_subu),
    .ori(instructionrecognition_1_ori), .slt(instructionrecognition_1_slt), .lw(instructionrecognition_1_lw),
    .sw(instructionrecognition_1_sw), .beq(instructionrecognition_1_beq), .j(instructionrecognition_1_j),
    .jal(instructionrecognition_1_jal), .jr(instructionrecognition_1_jr), .NPCOp(NPCOp),
    .immExtOp(signalsender_1_immextop), .RFWE(out_3), .ALUOp(signalsender_1_aluop), .DMWE(out_6),
    .WRSel(WRSel), .RFWDSel(RFWDSel), .BSel(signalsender_1_bsel), .lui(instructionrecognition_1_lui),
    .\or (instructionrecognition_1_or), .add(instructionrecognition_1_add), .sub(instructionrecognition_1_sub));
  Multiplexer #(.width(32)) multiplexer_4 (
    .in0(out_8), .in1(ext_1_imm32), .out(multiplexer_4_out), .sel(signalsender_1_bsel));  // open: en
  ALU alu_1 (
    .A(rf_1_out1), .B(multiplexer_4_out), .out(MemAddr), .ALUOp(signalsender_1_aluop), .in_4(1'b1),
    .Zero(alu_1_zero));
  DM dm_1 (.address(MemAddr), .WD(out_8), .RD(dm_1_rd), .clk(clk), .RAMWE(out_6), .clr(in_1));
  // Probe on MemAddr
  // Probe on dm_1_rd
  // Probe on rf_1_out1
  // Probe on multiplexer_4_out
  Shifter #(.width(32), .shift("lr")) shifter_1 (.in(MemAddr), .\dist (5'b00010), .out(shifter_1_out));
  Bit_Extender #(.in_width(32), .out_width(5)) bit_extender_1 (.in(shifter_1_out), .out(out_7));

  // Other names for the same wires on the sheet: clr = in_1; Instr[31:0] = out_2; MemData[31:0] = out_8;
  //   MemWrite = out_6; RagAddr[4:0] = out_4; RagData[31:0] = out_5; RagWrite = out_3

  // Notes on the sheet:
  //   imm16 when beq
  //   add26 when j | jal
  //   BeqYes?
  //   immEXTOp
  //   writeBack
  //   RA when jr
  //   RFWE
  //   BSel
  //   ALUOp
  //   DMWE
endmodule

module PC (
  input  [31:0] NPC,
  input  clk,
  input  clr,
  output [31:0] PC
);

  Register #(.width(32)) register_1 (.D(NPC), .Q(PC), .clk(clk), .clr(clr));  // open: en
endmodule

module NPC (
  input  [2:0] NPCOp,
  input  BeqYes,
  input  [31:0] PC,
  input  [25:0] imm26,
  input  [31:0] ra,
  output [31:0] PC4,
  output [31:0] NPC
);

  wire [31:0] adder_2_out, bit_extender_1_out, multiplexer_1_out;

  assign bit_extender_1_out = {{6{imm26[25]}}, imm26};  // Bit_Extender bit_extender_1
  Adder #(.width(32)) adder_1 (.a(PC), .b(32'h1), .out(PC4));  // open: cin, cout
  Shifter #(.width(32)) shifter_1 (.in(bit_extender_1_out), .\dist (5'b00010));  // open: out
  Adder #(.width(32)) adder_2 (.a(PC4), .b(bit_extender_1_out), .out(adder_2_out));  // open: cin, cout
  Multiplexer #(.width(32)) multiplexer_1 (
    .in0(PC4), .in1(adder_2_out), .out(multiplexer_1_out), .sel(BeqYes));  // open: en
  Multiplexer #(.select(3), .width(32)) multiplexer_2 (
    .in0(PC4), .in1(multiplexer_1_out), .in2(bit_extender_1_out), .in3(bit_extender_1_out), .in4(ra),
    .out(NPC), .sel(NPCOp));  // open: in5, in6, in7, en
endmodule

module IM (
  input  [31:0] address,
  output [31:0] instruction
);

  wire [7:0] bit_extender_1_out;

  Bit_Extender #(.in_width(32), .out_width(8)) bit_extender_1 (.in(address), .out(bit_extender_1_out));
  ROM #(.dataWidth(32)) rom_1 (.addr(bit_extender_1_out), .data(instruction));  // open: sel

  // Notes on the sheet:
  //   contents of rom_1 (hex, n*v repeats v):
  //   341c0000 341d0000 34013456 210820 8c010004 ac010004 3c027878 411822 3c051234 34040005 0 ac85ffff
  //   8c83ffff 10650001 1000000d 34670404 10e3000b 0 3c087777 3508ffff 80022 34001100 e65020 34080000
  //   34090001 340a0001 10a4020 1109fffe 1000ffff
endmodule

module InstrcutionSplitter (
  input  [31:0] instruction,
  output [5:0] opcode,
  output [4:0] rs,
  output [4:0] rt,
  output [4:0] rd,
  output [4:0] shamt,
  output [5:0] funct,
  output [15:0] imm16,
  output [25:0] address
);


  assign address = instruction[25:0];
  assign funct = instruction[5:0];
  assign imm16 = instruction[15:0];
  assign opcode = instruction[31:26];
  assign rd = instruction[15:11];
  assign rs = instruction[25:21];
  assign rt = instruction[20:16];
  assign shamt = instruction[10:6];
endmodule

module RF (
  input  clk,
  input  reset,
  input  en,
  input  [4:0] address1,
  input  [4:0] address2,
  input  [4:0] address3,
  input  [31:0] in,
  output [31:0] out1,
  output [31:0] out2
);

  wire [31:0] _0, _1, _2, _3, _4, _5, _6, _7, _8, _9, _10, _11, _12, _13, _14, _15, _16, _17, _18, _19, _20,
       _21, _22, _23, _24, _25, _26, _27, _28, _29, _30, _31, a0, a1, a2, a3, a4, a5, a6, a7, a8, a9, a10,
       a11, a12, a13, a14, a15, a16, a17, a18, a19, a20, a21, a22, a23, a24, a25, a26, a27, a28, a29, a30,
       a31;

  Demultiplexer #(.select(5), .width(32), .tristate("true")) demultiplexer_1 (
    .out0(_0), .out1(_1), .out2(_2), .out3(_3), .out4(_4), .out5(_5), .out6(_6), .out7(_7), .out8(_8),
    .out9(_9), .out10(_10), .out11(_11), .out12(_12), .out13(_13), .out14(_14), .out15(_15), .out16(_16),
    .out17(_17), .out18(_18), .out19(_19), .out20(_20), .out21(_21), .out22(_22), .out23(_23), .out24(_24),
    .out25(_25), .out26(_26), .out27(_27), .out28(_28), .out29(_29), .out30(_30), .out31(_31), .in(in),
    .sel(address3));  // open: en
  Register #(.width(32)) u__0 (.en(en), .Q(a0), .clk(clk), .clr(reset));  // open: D
  Register #(.width(32)) u__4 (.D(_4), .en(en), .Q(a4), .clk(clk), .clr(reset));
  Register #(.width(32)) u__8 (.D(_8), .en(en), .Q(a8), .clk(clk), .clr(reset));
  Register #(.width(32)) u__12 (.D(_12), .en(en), .Q(a12), .clk(clk), .clr(reset));
  Register #(.width(32)) u__16 (.D(_16), .en(en), .Q(a16), .clk(clk), .clr(reset));
  Register #(.width(32)) u__20 (.D(_20), .en(en), .Q(a20), .clk(clk), .clr(reset));
  Register #(.width(32)) u__24 (.D(_24), .en(en), .Q(a24), .clk(clk), .clr(reset));
  Register #(.width(32)) u__28 (.D(_28), .en(en), .Q(a28), .clk(clk), .clr(reset));
  Register #(.width(32)) u__1 (.D(_1), .en(en), .Q(a1), .clk(clk), .clr(reset));
  Register #(.width(32)) u__5 (.D(_5), .en(en), .Q(a5), .clk(clk), .clr(reset));
  Register #(.width(32)) u__9 (.D(_9), .en(en), .Q(a9), .clk(clk), .clr(reset));
  Register #(.width(32)) u__13 (.D(_13), .en(en), .Q(a13), .clk(clk), .clr(reset));
  Register #(.width(32)) u__17 (.D(_17), .en(en), .Q(a17), .clk(clk), .clr(reset));
  Register #(.width(32)) u__21 (.D(_21), .en(en), .Q(a21), .clk(clk), .clr(reset));
  Register #(.width(32)) u__25 (.D(_25), .en(en), .Q(a25), .clk(clk), .clr(reset));
  Register #(.width(32)) u__29 (.D(_29), .en(en), .Q(a29), .clk(clk), .clr(reset));
  Register #(.width(32)) u__2 (.D(_2), .en(en), .Q(a2), .clk(clk), .clr(reset));
  Register #(.width(32)) u__6 (.D(_6), .en(en), .Q(a6), .clk(clk), .clr(reset));
  Register #(.width(32)) u__10 (.D(_10), .en(en), .Q(a10), .clk(clk), .clr(reset));
  Register #(.width(32)) u__14 (.D(_14), .en(en), .Q(a14), .clk(clk), .clr(reset));
  Register #(.width(32)) u__18 (.D(_18), .en(en), .Q(a18), .clk(clk), .clr(reset));
  Register #(.width(32)) u__22 (.D(_22), .en(en), .Q(a22), .clk(clk), .clr(reset));
  Register #(.width(32)) u__26 (.D(_26), .en(en), .Q(a26), .clk(clk), .clr(reset));
  Register #(.width(32)) u__30 (.D(_30), .en(en), .Q(a30), .clk(clk), .clr(reset));
  Register #(.width(32)) u__3 (.D(_3), .en(en), .Q(a3), .clk(clk), .clr(reset));
  Register #(.width(32)) u__7 (.D(_7), .en(en), .Q(a7), .clk(clk), .clr(reset));
  Register #(.width(32)) u__11 (.D(_11), .en(en), .Q(a11), .clk(clk), .clr(reset));
  Register #(.width(32)) u__15 (.D(_15), .en(en), .Q(a15), .clk(clk), .clr(reset));
  Register #(.width(32)) u__19 (.D(_19), .en(en), .Q(a19), .clk(clk), .clr(reset));
  Register #(.width(32)) u__23 (.D(_23), .en(en), .Q(a23), .clk(clk), .clr(reset));
  Register #(.width(32)) u__27 (.D(_27), .en(en), .Q(a27), .clk(clk), .clr(reset));
  Register #(.width(32)) u__31 (.D(_31), .en(en), .Q(a31), .clk(clk), .clr(reset));
  Multiplexer #(.select(5), .width(32)) multiplexer_1 (
    .in0(a0), .in1(a1), .in2(a2), .in3(a3), .in4(a4), .in5(a5), .in6(a6), .in7(a7), .in8(a8), .in9(a9),
    .in10(a10), .in11(a11), .in12(a12), .in13(a13), .in14(a14), .in15(a15), .in16(a16), .in17(a17),
    .in18(a18), .in19(a19), .in20(a20), .in21(a21), .in22(a22), .in23(a23), .in24(a24), .in25(a25),
    .in26(a26), .in27(a27), .in28(a28), .in29(a29), .in30(a30), .in31(a31), .out(out1), .sel(address1));  // open: en
  Multiplexer #(.select(5), .width(32)) multiplexer_2 (
    .in0(a0), .in1(a1), .in2(a2), .in3(a3), .in4(a4), .in5(a5), .in6(a6), .in7(a7), .in8(a8), .in9(a9),
    .in10(a10), .in11(a11), .in12(a12), .in13(a13), .in14(a14), .in15(a15), .in16(a16), .in17(a17),
    .in18(a18), .in19(a19), .in20(a20), .in21(a21), .in22(a22), .in23(a23), .in24(a24), .in25(a25),
    .in26(a26), .in27(a27), .in28(a28), .in29(a29), .in30(a30), .in31(a31), .out(out2), .sel(address2));  // open: en
endmodule

module ALU (
  input  [3:0] ALUOp,
  input  [31:0] A,
  input  [31:0] B,
  input  in_4,
  output [31:0] out,
  output Zero
);

  wire comparator_1_lt;
  wire [31:0] add, lui, \or , ori, slt, sub;

  Adder #(.width(32)) adder_1 (.a(A), .b(B), .out(add));  // open: cin, cout
  Subtractor #(.width(32)) subtractor_1 (.a(A), .b(B), .out(sub));  // open: bin, bout
  assign ori = A | B;  // OR_Gate or_1, 32 bits wide
  Shifter #(.width(32)) shifter_1 (.in(B), .\dist (5'b10000), .out(lui));
  assign \or  = A | B;  // OR_Gate or_2, 32 bits wide
  Comparator #(.width(32)) comparator_1 (.a(A), .b(B), .eq(Zero), .lt(comparator_1_lt));  // open: gt
  assign slt = {{31{1'b0}}, comparator_1_lt};  // Bit_Extender bit_extender_1
  Multiplexer #(.select(4), .width(32)) multiplexer_1 (
    .in0(add), .in1(sub), .in2(ori), .in3(slt), .in4(add), .in5(add), .in6(lui), .in7(\or ), .in8(add),
    .in9(sub), .out(out), .sel(ALUOp), .en(in_4));  // open: in10, in11, in12, in13, in14, in15

  // Other names for the same wires on the sheet: subu[31:0] = sub; addu[31:0] = add; lw[31:0] = add; sw[31:0] = add
endmodule

module DM (
  input  [31:0] address,
  input  [31:0] WD,
  input  RAMWE,
  input  clk,
  input  clr,
  output [31:0] RD
);

  wire [7:0] bit_extender_1_out;
  wire [31:0] shifter_1_out;

  Shifter #(.width(32), .shift("lr")) shifter_1 (.in(address), .\dist (5'b00010), .out(shifter_1_out));
  Bit_Extender #(.in_width(32), .out_width(8)) bit_extender_1 (.in(shifter_1_out), .out(bit_extender_1_out));
  RAM #(.dataWidth(32), .bus("separate")) ram_1 (
    .addr(bit_extender_1_out), .din(WD), .data(RD), .str(RAMWE), .clk(clk), .clr(clr));  // open: sel, ld
endmodule

module InstructionRecognition (
  input  [5:0] opcode,
  input  [5:0] funct,
  output ori,
  output lw,
  output sw,
  output beq,
  output j,
  output jal,
  output lui,
  output addu,
  output subu,
  output slt,
  output jr,
  output add,
  output \or ,
  output sub
);

  wire not_1_out, not_2_out, not_3_out, not_4_out, not_5_out, not_6_out, not_7_out, not_8_out, not_9_out,
       not_10_out, not_11_out, not_12_out;

  not not_1 (not_1_out, opcode[5]);
  not not_2 (not_2_out, opcode[4]);
  not not_3 (not_3_out, opcode[3]);
  not not_4 (not_4_out, opcode[2]);
  not not_5 (not_5_out, opcode[1]);
  not not_6 (not_6_out, opcode[0]);
  not not_7 (not_7_out, funct[5]);
  not not_8 (not_8_out, funct[4]);
  not not_9 (not_9_out, funct[3]);
  not not_10 (not_10_out, funct[2]);
  not not_11 (not_11_out, funct[1]);
  not not_12 (not_12_out, funct[0]);
  and and_1 (ori, not_1_out, not_2_out, opcode[3], opcode[2], not_5_out, opcode[0]);
  and and_2 (addu, not_1_out, not_2_out, not_3_out, not_4_out, not_5_out, not_6_out, funct[5], not_8_out, not_9_out, not_10_out, not_11_out, funct[0]);
  and and_3 (lw, opcode[5], not_2_out, not_3_out, not_4_out, opcode[1], opcode[0]);
  and and_4 (subu, not_1_out, not_2_out, not_3_out, not_4_out, not_5_out, not_6_out, funct[5], not_8_out, not_9_out, not_10_out, funct[1], funct[0]);
  and and_5 (sw, opcode[5], not_2_out, opcode[3], not_4_out, opcode[1], opcode[0]);
  and and_6 (slt, not_1_out, not_2_out, not_3_out, not_4_out, not_5_out, not_6_out, funct[5], not_8_out, funct[3], not_10_out, funct[1], not_12_out);
  and and_7 (jr, not_1_out, not_2_out, not_3_out, not_4_out, not_5_out, not_6_out, not_7_out, not_8_out, funct[3], not_10_out, not_11_out, not_12_out);
  and and_8 (beq, not_1_out, not_2_out, not_3_out, opcode[2], not_5_out, not_6_out);
  and and_9 (j, not_1_out, not_2_out, not_3_out, not_4_out, opcode[1], not_6_out);
  and and_10 (add, not_1_out, not_2_out, not_3_out, not_4_out, not_5_out, not_6_out, funct[5], not_8_out, not_9_out, not_10_out, not_11_out, not_12_out);
  and and_11 (jal, not_1_out, not_2_out, not_3_out, not_4_out, opcode[1], opcode[0]);
  and and_12 (lui, not_1_out, not_2_out, opcode[3], opcode[2], opcode[1], opcode[0]);
  and and_13 (\or , not_1_out, not_2_out, not_3_out, not_4_out, not_5_out, not_6_out, funct[5], not_8_out, not_9_out, funct[2], not_11_out, funct[0]);
  and and_14 (sub, not_1_out, not_2_out, not_3_out, not_4_out, not_5_out, not_6_out, funct[5], not_8_out, not_9_out, not_10_out, funct[1], not_12_out);
endmodule

module SignalSender (
  input  sub,
  input  add,
  input  \or ,
  input  addu,
  input  subu,
  input  ori,
  input  slt,
  input  lw,
  input  sw,
  input  beq,
  input  j,
  input  jal,
  input  jr,
  input  lui,
  output [2:0] NPCOp,
  output immExtOp,
  output RFWE,
  output [3:0] ALUOp,
  output DMWE,
  output [1:0] WRSel,
  output [1:0] RFWDSel,
  output BSel
);

  or or_1 (NPCOp[1], j, jal);
  or or_2 (NPCOp[0], beq, jal);
  or or_3 (immExtOp, lw, sw);
  or or_4 (RFWE, add, \or , addu, subu, ori, slt, lw, jal, lui, sub);
  or or_5 (ALUOp[3], sub, add);
  or or_6 (ALUOp[2], lui, sw, lw, \or );
  or or_7 (ALUOp[1], lui, slt, ori, \or );
  or or_8 (ALUOp[0], sw, slt, sub, subu, \or );
  or or_9 (WRSel[0], slt, subu, addu, \or , add, sub);
  or or_10 (BSel, sw, lui, ori, lw);

  assign DMWE = sw;
  assign NPCOp[2] = jr;
  assign RFWDSel = {jal, lw};
  assign WRSel[1] = jal;
endmodule

module EXT (
  input  [15:0] imm16,
  input  ExtOp,
  output [31:0] imm32
);

  wire [31:0] bit_extender_1_out, bit_extender_2_out;

  assign bit_extender_1_out = {{16{1'b0}}, imm16};  // Bit_Extender bit_extender_1
  assign bit_extender_2_out = {{16{imm16[15]}}, imm16};  // Bit_Extender bit_extender_2
  Multiplexer #(.width(32)) multiplexer_1 (
    .in0(bit_extender_1_out), .in1(bit_extender_2_out), .out(imm32), .sel(ExtOp));  // open: en
endmodule
